// Digital circuit cpu.dig as structural Verilog
module cpu (
  input  in_1,
  input  in_2
);

  wire IC_o_0, IC_o_1, IC_o_2, IC_o_3, madr_q_0, madr_q_1, madr_q_2, madr_q_3, tri_state_buffer_4bit_1_o_0,
       tri_state_buffer_4bit_1_o_1, tri_state_buffer_4bit_1_o_2, tri_state_buffer_4bit_1_o_3;

  DipSwitch #(.dipDefault("true")) dipswitch_1 ();  // open: out
  register_simple madr (
    .D_0(tri_state_buffer_4bit_1_o_0), .D_1(tri_state_buffer_4bit_1_o_1), .D_2(tri_state_buffer_4bit_1_o_2),
    .D_3(tri_state_buffer_4bit_1_o_3), .Q_0(madr_q_0), .Q_1(madr_q_1), .Q_2(madr_q_2), .Q_3(madr_q_3));  // open: E_out, CLK
  tri_state_buffer_4bit tri_state_buffer_4bit_1 (
    .D_0(madr_q_0), .D_1(madr_q_1), .D_2(madr_q_2), .D_3(madr_q_3), .E(in_2),
    .O_0(tri_state_buffer_4bit_1_o_0), .O_1(tri_state_buffer_4bit_1_o_1), .O_2(tri_state_buffer_4bit_1_o_2),
    .O_3(tri_state_buffer_4bit_1_o_3));
  tri_state_buffer_4bit tri_state_buffer_4bit_2 (
    .D_0(IC_o_0), .D_1(IC_o_1), .D_2(IC_o_2), .D_3(IC_o_3), .E(in_1), .O_0(tri_state_buffer_4bit_1_o_0),
    .O_1(tri_state_buffer_4bit_1_o_1), .O_2(tri_state_buffer_4bit_1_o_2), .O_3(tri_state_buffer_4bit_1_o_3));
  counter IC (.O_0(IC_o_0), .O_1(IC_o_1), .O_2(IC_o_2), .O_3(IC_o_3));  // open: C

  // Notes on the sheet:
  //   clock
  //   fibonnacci (n):
  //   # if < 2 can be erased if required n >= 2
  //   if n < 2 -> n
  //   smaller <- 0
  //   bigger <- 1
  //   until n > 0 do
  //   .  tmp <- bigger
  //   .  bigger <- smaller+bigger
  //   .  smaller <- tmp
  //   .  n--
  //   return bigger
  //   fibonnacci (n):
  //   set adr of smaller ($00) <- 0
  //   set adr of bigger ($01) <- 1
  //   set adr of n ($10) <- n
  //   until n > 0 do
  //   .  tmp <- bigger (mov $bigger, A; mov A, $tmp)
  //   .  bigger <- smaller+bigger (mov $smaller, B; save ALU to $bigger)
  //   .  smaller <- tmp
  //   .  n--      (n - 1; jne)
  //   return bigger
  //   microinstruction counter
  //   memory adr register
  //   Instruction Counter
  //   microinstruction memory optimizer?
  //   microinstructions memory
  //   memory
  //   instruction register
  //   register A
  //   register B
  //   CPU control word: IC r/w/inc, mem adr R, IR r, mem r/w, reg a r/w, reg b r/w, ALU w
  //   ALU
  //   clock: 1
  //   read and increase ms counter ->
  //   get control word from ms memory (maybe normalize address first in memory optimizer) ->
  //   output 1st CPU control word: 
  //   read and increase instruction counter | write memory adr register 
  //   clock 2: 1st cpu control word is executed:
  //   read and increase IC, 
  //   store value in memory adr reg, 
  //   memory instantly puts result into IR, 
  //   based on IR lookup in ms memory is done
  //   2nd cpu control word is ready
  //   2-complementary:
  //   0111   7
  //   ...
  //   0100   4
  //   0011    3
  //   0010    2
  //   0001    1
  //   0000    0
  //   1111   -1
  //   1110   -2
  //   1101   -3
  //   1100   -4
  //   ...
  //   1001  -7
  //   1000  -8
  //   + 0001   1
  //   .  1111   -1
  //   -------------
  //     10000  0
  //   0010
  //   1110
endmodule
